# Fritzing sketch Schéma électrique (saved by Fritzing 0.9.3b)
breadboards: 1

parts:
  Composant1 = NRF24L01+ Breakout Board  # not connected
  Composant2 = NRF24L01+ Breakout Board
  Composant3 = Arduino Mega 2560 (Rev3)
  M1 = DC Motor  # not connected
  M2 = DC Motor
  L1 = Solenoid
  L2 = Solenoid
  L3 = Solenoid
  L4 = Solenoid
  U2 = LIPO-2000mAh [package=lipo-2000]
  Q1 = NPN-Transistor [package="SOT-23 [SMD]"]
  Q2 = NPN-Transistor [package="SOT-23 [SMD]"]
  Q3 = NPN-Transistor [package="SOT-23 [SMD]"]
  ANT1 = Antenna
  Composant4 = Thumb Joystick
  J1 = Basic Servo
  Composant6 = Arduino Nano (Rev3.0) (ICSP)
  M3 = DC Motor  # not connected
  M4 = DC Motor  # not connected
  L298N1 = L298N DC motor driver

nets:
  GND: Composant2.GND, Composant6.GND
  VCC: Composant2.VCC, Composant6.5V
  N1: Composant2.CE, Composant6.D9
  N2: Composant2.CS, Composant6.D8
  N3: Composant2.SCK, Composant6.D10
  N4: Composant2.MOSI, Composant6.D7
  N5: Composant2.MISO, Composant6.D11/MOSI
  N6: Composant2.IRQ, Composant6.D6
  N7: Composant3.A0, Composant4.VERT
  N8: Composant3.A1, Composant4.HORZ
  VCC_2: Composant3.5V, Composant4.VCC, J1.vcc
  GND_2: Composant3.GND, Q1.1, Q2.1, Q3.1, Composant4.GND, J1.gnd, L298N1.GND
  N9: Composant3.D3_PWM, J1.pulse
  N10: Composant3.D4_PWM, Composant4.SEL
  N11: Composant3.D5_PWM, Q3.0
  N12: Composant3.D6_PWM, Q2.0
  N13: Composant3.D7_PWM, Q1.0
  N14: Composant3.D45, L298N1.IN1
  N15: Composant3.D47, L298N1.IN2
  N16: Composant3.D49, L298N1.IN3
  N17: Composant3.D51, L298N1.IN4
  N18: M2.pin_1, ANT1.antenna_lead
  N19: L1.pin1, L2.pin1, Q1.2
  N20: L1.pin2, L2.pin2, L3.pin2, L4.pin2, U2.+, L298N1.12V
  N21: L3.pin1, Q3.2
  N22: L4.pin1, Q2.2

notes:
  Treuil M2
  Treuil M1
  Vérins
  Vérin Mât M4
  Vérin mat de grande vergue M3
  Vérin de la croix X2 M6 et M7
  MB : Moteurs Brushless

custom parts:
  L298N DC motor driver: 2x DC motor driver with 78M05 positive voltage regulator (7..35 V) L298N: max 46 V, 2 A Set 5 V Enable jumper to enable 5 V regultor (needed for the L298N) and +5 V output at screw terminal or supply external +5 V at screw terminal Set ENA and/or ENB to +5 V to enable motor permanently or supply ENA and/or ENB with PWM signal IN1 and IN2 set rotation directory for motor A (OUT1/OUT2) IN2 and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

// code stored in the sketch: Untitled2.ino
void setup()
{
  pinMode(7, OUTPUT);
}

void loop()
{
  analogWrite(7, 0);
  delay(1000); // Wait for 1000 millisecond(s)
  analogWrite(7,127);
  delay(1000);
  analogWrite(7, 255);
  delay(1000); // Wait for 1000 millisecond(s)
}
